# Fritzing sketch example_wiring_diagram (saved by Fritzing 0.9.2b)

parts:
  BATT1 = 4xAA Switchable Battery Pack w/Bare Wire  # not connected
  LED1 = smd LED [color="Green (555nm)" package="1206 [SMD]"]
  LED5 = LED - 5mm [color="Red (635nm)" package="5 mm [THT]"]
  R1 = Resistor [tolerance=±5% resistance=100 package=THT]

nets:
  N1: LED1.cathode, LED5.anode
  N2: LED1.anode, R1.Pin_1

notes:
  100 Ohm

custom parts:
  4xAA Switchable Battery Pack w/Bare Wire: 4xAA Switchable Battery Pack with Bare Wire connection
